# Fritzing sketch SandCastle (saved by Fritzing 0.9.1b)

parts:
  Part1 = Arduino Uno (Rev3) - ICSP
  U1 = RF-LINK_RX [package=rf-link_rx]

nets:
  N1: Part1.ICSP_MOSI, Part1.D11_PWM/MOSI, U1.+5V
  N2: Part1.D13/SCK, U1.DATA
  GND: Part1.GND, U1.GND

notes:
  Antenna - 24cm wire
  You can plug the receiver directly into the Arduino.
  Just don't forget to cut the CS pin.
