# Fritzing sketch SenseGrain (saved by Fritzing 0.9.1b)
breadboards: 1

parts:
  BAT1 = Battery Holders [package=battcom_20mm_pth]
  U1 = ATTINY45 [package=dip]
  S1 = Pushbutton [package="[THT]"]
  R1 = PHOTOCELL [package=photocell]
  U2 = RF-LINK_TX [package=rf-link_tx]
  R2 = TRIMPOT [package=3386u]
  R3 = Resistor [tolerance=±5% resistance=10k package="0805 [SMD]"]

nets:
  GND: BAT1.+, U1.GND, S1.Pin_3, S1.Pin_4, U2.GND, R2.CW, R3.Pin_0
  VCC: BAT1.-, U1.VCC, U2.+5V
  N1: U1.PB3(ADC3), S1.Pin_1, S1.Pin_2
  N2: U1.PB4(ADC2), R1.P$1, R3.Pin_1
  N3: U1.PB0(MOSI), U2.DATA
  N4: U1.PB1(MISO), R1.P$2, R2.CCW
  N5: U1.PB2(SCK_ADC1), R2.WIPER

notes:
  Antenna
  24cm wire
  <-- Example
  Sensor
  Transmitter
